# Fritzing sketch x16relay (saved by Fritzing 0.9.3b)
breadboards: 1

parts:
  MC1 = ESP8266 WiFi Module [part_number=ESP8266]
  IC1 = MCP23017 I2C I/O Expander
  JACK2 = 2.1mm Barrel Jack with Terminal Block
  U1 = RELAY [package=relay-t9a]
  U2 = RELAY [package=relay-t9a]
  U3 = RELAY [package=relay-t9a]
  U4 = RELAY [package=relay-t9a]
  U5 = RELAY [package=relay-t9a]
  U6 = RELAY [package=relay-t9a]
  U7 = RELAY [package=relay-t9a]
  U8 = RELAY [package=relay-t9a]
  U9 = RELAY [package=relay-t9a]
  U10 = RELAY [package=relay-t9a]
  U11 = RELAY [package=relay-t9a]
  U12 = RELAY [package=relay-t9a]
  U13 = RELAY [package=relay-t9a]
  U14 = RELAY [package=relay-t9a]
  U15 = RELAY [package=relay-t9a]
  U16 = RELAY [package=relay-t9a]

nets:
  VCC: MC1.VCC, IC1.VDD, IC1.RESET, JACK2.POS
  N1: MC1.GPIO_0, IC1.SDA
  N2: MC1.GPIO_2, IC1.SCL
  GND: MC1.GND, IC1.VSS, IC1.A0, IC1.A1, IC1.A2, JACK2.NEG, U1.COIL2, U2.COIL2, U3.COIL2, U4.COIL2, U5.COIL2, U6.COIL2, U7.COIL2, U8.COIL2, U9.COIL2, U10.COIL2, U11.COIL2, U12.COIL2, U13.COIL2, U14.COIL2, U15.COIL2, U16.COIL2
  N3: IC1.GPB0, U9.COIL1
  N4: IC1.GPB1, U10.COIL1
  N5: IC1.GPB2, U11.COIL1
  N6: IC1.GPB3, U12.COIL1
  N7: IC1.GPB4, U13.COIL1
  N8: IC1.GPB5, U14.COIL1
  N9: IC1.GPB6, U15.COIL1
  N10: IC1.GPB7, U16.COIL1
  N11: IC1.GPA0, U1.COIL1
  N12: IC1.GPA1, U2.COIL1
  N13: IC1.GPA2, U3.COIL1
  N14: IC1.GPA3, U4.COIL1
  N15: IC1.GPA4, U5.COIL1
  N16: IC1.GPA5, U6.COIL1
  N17: IC1.GPA6, U7.COIL1
  N18: IC1.GPA7, U8.COIL1

custom parts:
  MCP23017 I2C I/O Expander: The MCP23017 uses two i2c pins (these can be shared with other i2c devices), and in exchange gives you 16 general purpose pins. You can set each of 16 pins to be input, output, input with a pullup or open drain. There's even the ability to get an interrupt via an external pin when any of the inputs change so you don't have to keep polling the chip.
