# Fritzing sketch nfc (saved by Fritzing 0.9.3b)

parts:
  MC = ESP8266 WiFi Module [part_number=ESP8266]
  Part1 = 16 NeoPixel Ring [part_number=1463]
  NFC_Reader = Adafruit PN532 Breakout [part_number=PN532]
  C1 = Ceramic Capacitor [capacitance=1mF package="200 mil [THT, multilayer]"]
  R1 = Resistor [tolerance=±5% resistance=470 package=THT]
  JACK1 = 2.1mm Barrel Jack with Terminal Block

nets:
  3.3V: MC.VCC, Part1.VDD, NFC_Reader.VDD, C1.0, JACK1.POS
  N1: MC.GPIO_2, NFC_Reader.NSS/SCL/RX
  GND: MC.GND, Part1.GND, NFC_Reader.GND, C1.1, JACK1.NEG
  N2: MC.GPIO_5, R1.Pin_0
  N3: MC.GPIO_14, NFC_Reader.SCK
  N4: MC.GPIO_12, NFC_Reader.MISO
  N5: MC.GPIO_13, NFC_Reader.MOSI/SDA/TX
  N6: Part1.IN, R1.Pin_1

custom parts:
  16 NeoPixel Ring: 16 ultra bright smart LED NeoPixels are arranged in a circle with 1.75" (44.5mm) outer diameter. The rings are 'chainable' - connect the output pin of one to the input pin of another. Use only one microcontroller pin to control as many as you can chain together! Each LED is addressable as the driver chip is inside the LED. Each one has ~18mA constant current drive so the color will be very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
  Adafruit PN532 Breakout: The PN532 is the most popular NFC chip, and is what is embedded in pretty much every phone or device that does NFC. It can pretty much do it all, such as read and write to tags and cards, communicate with phones (say for payment processing), and 'act' like a NFC tag. If you want to do any sort of embedded NFC work, this is the chip you'll want to use! NFC (Near Field Communications) is a way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
